// Logisim project ETFExtended.circ as structural Verilog: 8 circuits, main circuit INTERRUPT_INTERFACE_4
module INTERRUPT_INTERFACE_4 (
  input  BTN_INTR0,
  input  BTN_INTR1,
  input  BTN_INTR2,
  input  BTN_INTR3,
  input  inta,
  input  [1:0] UEXT,
  input  CLK,
  output [3:0] intr
);

  wire and_1_out, and_2_out, and_3_out, and_4_out, D0, D1, D2, D3;

  DC2_4 dc2_4_1 (.D0(D0), .D1(D1), .D2(D2), .D3(D3), .X(UEXT), .En(inta));
  and and_1 (and_1_out, D0, ~BTN_INTR0);  // AND_Gate
  and and_2 (and_2_out, D1, ~BTN_INTR1);  // AND_Gate
  and and_3 (and_3_out, D2, ~BTN_INTR2);  // AND_Gate
  and and_4 (and_4_out, D3, ~BTN_INTR3);  // AND_Gate
  RSFF rsff_1 (.Q(intr[0]), .S(BTN_INTR0), .R(and_1_out), .CLK(CLK));  // open: notQ, Sd, Rd
  RSFF rsff_2 (.Q(intr[1]), .S(BTN_INTR1), .R(and_2_out), .CLK(CLK));  // open: notQ, Sd, Rd
  RSFF rsff_3 (.Q(intr[2]), .S(BTN_INTR2), .R(and_3_out), .CLK(CLK));  // open: notQ, Sd, Rd
  RSFF rsff_4 (.Q(intr[3]), .S(BTN_INTR3), .R(and_4_out), .CLK(CLK));  // open: notQ, Sd, Rd
endmodule

module INTERRUPT_INTERFACE_8 (
  input  BTN_INTR0,
  input  BTN_INTR1,
  input  BTN_INTR2,
  input  BTN_INTR3,
  input  BTN_INTR4,
  input  BTN_INTR5,
  input  BTN_INTR6,
  input  BTN_INTR7,
  input  inta,
  input  [2:0] UEXT,
  input  CLK,
  output [7:0] intr
);

  wire and_1_out, and_2_out, and_3_out, and_4_out, and_5_out, and_6_out, and_7_out, and_8_out, D0, D1, D2,
       D3, D4, D5, D6, D7;

  DC3_8 dc3_8_1 (.D0(D0), .D1(D1), .D2(D2), .D3(D3), .D4(D4), .D5(D5), .D6(D6), .D7(D7), .X(UEXT), .En(inta));
  and and_1 (and_1_out, D0, ~BTN_INTR0);  // AND_Gate
  and and_2 (and_2_out, D1, ~BTN_INTR1);  // AND_Gate
  and and_3 (and_3_out, D2, ~BTN_INTR2);  // AND_Gate
  and and_4 (and_4_out, D3, ~BTN_INTR3);  // AND_Gate
  and and_5 (and_5_out, D4, ~BTN_INTR4);  // AND_Gate
  and and_6 (and_6_out, D5, ~BTN_INTR5);  // AND_Gate
  and and_7 (and_7_out, D6, ~BTN_INTR6);  // AND_Gate
  and and_8 (and_8_out, D7, ~BTN_INTR7);  // AND_Gate
  RSFF rsff_1 (.Q(intr[0]), .S(BTN_INTR0), .R(and_1_out), .CLK(CLK));  // open: notQ, Sd, Rd
  RSFF rsff_2 (.Q(intr[1]), .S(BTN_INTR1), .R(and_2_out), .CLK(CLK));  // open: notQ, Sd, Rd
  RSFF rsff_3 (.Q(intr[2]), .S(BTN_INTR2), .R(and_3_out), .CLK(CLK));  // open: notQ, Sd, Rd
  RSFF rsff_4 (.Q(intr[3]), .S(BTN_INTR3), .R(and_4_out), .CLK(CLK));  // open: notQ, Sd, Rd
  RSFF rsff_5 (.Q(intr[4]), .S(BTN_INTR4), .R(and_5_out), .CLK(CLK));  // open: notQ, Sd, Rd
  RSFF rsff_6 (.Q(intr[5]), .S(BTN_INTR5), .R(and_6_out), .CLK(CLK));  // open: notQ, Sd, Rd
  RSFF rsff_7 (.Q(intr[6]), .S(BTN_INTR6), .R(and_7_out), .CLK(CLK));  // open: notQ, Sd, Rd
  RSFF rsff_8 (.Q(intr[7]), .S(BTN_INTR7), .R(and_8_out), .CLK(CLK));  // open: notQ, Sd, Rd
endmodule

module ROM16x17 (
  input  [3:0] A,
  input  CS,
  output [16:0] DOUT
);

  wire [16:0] rom_1_data;

  ROM #(.addrWidth(4), .dataWidth(17)) rom_1 (.addr(A), .data(rom_1_data));
  assign DOUT = CS ? rom_1_data : 17'bz;  // Controlled_Buffer controlled_buffer_1
endmodule

module ROM16x24 (
  input  [3:0] A,
  input  CS,
  output [23:0] DOUT
);

  wire [23:0] rom_1_data;

  ROM #(.addrWidth(4), .dataWidth(24)) rom_1 (.addr(A), .data(rom_1_data));
  assign DOUT = CS ? rom_1_data : 24'bz;  // Controlled_Buffer controlled_buffer_1
endmodule

module ROM16x26 (
  input  [3:0] A,
  input  CS,
  output [25:0] DOUT
);

  wire [5:4] undriven;
  wire [36:0] rom_1_data;

  ROM #(.addrWidth(6), .dataWidth(37)) rom_1 (.addr({undriven, A}), .data(rom_1_data));
  assign DOUT = CS ? rom_1_data[25:0] : 26'bz;  // Controlled_Buffer controlled_buffer_1
  // Pins of 4 and 6 bits meet at {undriven, A}
  // Pins of 26 and 37 bits meet at rom_1_data
endmodule

module ROM64x37 (
  input  [5:0] A,
  input  CS,
  output [36:0] DOUT
);

  wire [36:0] rom_1_data;

  ROM #(.addrWidth(6), .dataWidth(37)) rom_1 (.addr(A), .data(rom_1_data));
  assign DOUT = CS ? rom_1_data : 37'bz;  // Controlled_Buffer controlled_buffer_1
endmodule

module GPR8x16 (
  input  [15:0] DI,
  input  [2:0] A,
  input  WR,
  input  CLK,
  output [15:0] DO
);

  wire and_1_out, and_2_out, and_3_out, and_4_out, and_5_out, and_6_out, and_7_out, and_8_out, CS0, CS1, CS2,
       CS3, CS4, CS5, CS6, CS7;
  wire [15:0] reg16_ld_1_a, reg16_ld_2_a, reg16_ld_3_a, reg16_ld_4_a, reg16_ld_5_a, reg16_ld_6_a,
       reg16_ld_7_a, reg16_ld_8_a;

  DC3_8 dc3_8_1 (.D0(CS0), .D1(CS1), .D2(CS2), .D3(CS3), .D4(CS4), .D5(CS5), .D6(CS6), .D7(CS7), .X(A), .En(1'b1));
  REG16_LD reg16_ld_1 (.A(reg16_ld_1_a), .LD(and_1_out), .CLK(CLK), .I(DI));  // open: mr
  assign DO = CS0 ? reg16_ld_1_a : 16'bz;  // Controlled_Buffer controlled_buffer_1
  REG16_LD reg16_ld_2 (.A(reg16_ld_2_a), .LD(and_2_out), .CLK(CLK), .I(DI));  // open: mr
  assign DO = CS1 ? reg16_ld_2_a : 16'bz;  // Controlled_Buffer controlled_buffer_2
  REG16_LD reg16_ld_3 (.A(reg16_ld_3_a), .LD(and_3_out), .CLK(CLK), .I(DI));  // open: mr
  assign DO = CS2 ? reg16_ld_3_a : 16'bz;  // Controlled_Buffer controlled_buffer_3
  REG16_LD reg16_ld_4 (.A(reg16_ld_4_a), .LD(and_4_out), .CLK(CLK), .I(DI));  // open: mr
  assign DO = CS3 ? reg16_ld_4_a : 16'bz;  // Controlled_Buffer controlled_buffer_4
  and and_1 (and_1_out, CS0, WR);
  and and_2 (and_2_out, CS1, WR);
  and and_3 (and_3_out, CS2, WR);
  and and_4 (and_4_out, CS3, WR);
  and and_5 (and_5_out, CS4, WR);
  REG16_LD reg16_ld_5 (.A(reg16_ld_5_a), .LD(and_5_out), .CLK(CLK), .I(DI));  // open: mr
  assign DO = CS4 ? reg16_ld_5_a : 16'bz;  // Controlled_Buffer controlled_buffer_5
  and and_6 (and_6_out, CS5, WR);
  REG16_LD reg16_ld_6 (.A(reg16_ld_6_a), .LD(and_6_out), .CLK(CLK), .I(DI));  // open: mr
  assign DO = CS5 ? reg16_ld_6_a : 16'bz;  // Controlled_Buffer controlled_buffer_6
  and and_7 (and_7_out, CS6, WR);
  REG16_LD reg16_ld_7 (.A(reg16_ld_7_a), .LD(and_7_out), .CLK(CLK), .I(DI));  // open: mr
  assign DO = CS6 ? reg16_ld_7_a : 16'bz;  // Controlled_Buffer controlled_buffer_7
  and and_8 (and_8_out, CS7, WR);
  REG16_LD reg16_ld_8 (.A(reg16_ld_8_a), .LD(and_8_out), .CLK(CLK), .I(DI));  // open: mr
  assign DO = CS7 ? reg16_ld_8_a : 16'bz;  // Controlled_Buffer controlled_buffer_8

  // Other names for the same wires on the sheet: inREG[15:0] = DI; outREG[15:0] = DO
endmodule

module MP2_6b (
  input  En,
  input  [5:0] I0,
  input  [5:0] I1,
  input  S0,
  output [5:0] Y
);

  wire not_1_out;
  wire [5:0] and_1_out, and_2_out, bit_extender_1_out, bit_extender_2_out, bit_extender_3_out, or_1_out;

  Pull_Resistor #(.pull(1)) pull_resistor_1 (.node(En));
  assign bit_extender_1_out = {{5{S0}}, S0};  // Bit_Extender bit_extender_1
  assign bit_extender_2_out = {{5{not_1_out}}, not_1_out};  // Bit_Extender bit_extender_2
  not not_1 (not_1_out, S0);
  assign and_1_out = I0 & bit_extender_2_out;  // AND_Gate and_1, 6 bits wide
  assign and_2_out = I1 & bit_extender_1_out;  // AND_Gate and_2, 6 bits wide
  assign bit_extender_3_out = {{5{En}}, En};  // Bit_Extender bit_extender_3
  assign or_1_out = and_1_out | and_2_out;  // OR_Gate or_1, 6 bits wide
  assign Y = bit_extender_3_out & or_1_out;  // AND_Gate and_3, 6 bits wide

  // Notes on the sheet:
  //   Ako En nije priključen (stanje visoke impednase - HiZ),
  //   uezti za podrazumevanu vrednost logičku jedinicu
  //   5..0
endmodule
