// Logisim project ETFStudent.circ as structural Verilog: 5 circuits, main circuit KMADR
module KMADR (
  input  immed,
  input  memdir,
  input  memind,
  input  regind,
  input  postincr,
  input  postdec,
  input  regdir,
  output [4:0] Adr
);

  assign Adr = immed ? 5'b00010 : 5'bz;  // Controlled_Buffer controlled_buffer_1
  assign Adr = memdir ? 5'b00011 : 5'bz;  // Controlled_Buffer controlled_buffer_2
  assign Adr = memind ? 5'b00100 : 5'bz;  // Controlled_Buffer controlled_buffer_3
  assign Adr = regind ? 5'b01001 : 5'bz;  // Controlled_Buffer controlled_buffer_4
  assign Adr = postincr ? 5'b01010 : 5'bz;  // Controlled_Buffer controlled_buffer_5
  assign Adr = postdec ? 5'b01011 : 5'bz;  // Controlled_Buffer controlled_buffer_6
  assign Adr = regdir ? 5'b10001 : 5'bz;  // Controlled_Buffer controlled_buffer_7
endmodule

module KMOPR (
  input  HALT,
  input  RTS,
  input  RTI,
  input  ROTR,
  input  ROTRC,
  input  PUSH,
  input  POP,
  input  BLEQ,
  input  BGREU,
  input  BNNG,
  input  BGRT,
  input  JLEQ,
  input  JSR,
  input  JMP,
  input  LD,
  input  ST,
  input  ADD,
  input  INC,
  input  LOR,
  input  STRFIND,
  output [6:0] Adr
);

  assign Adr = HALT ? 7'b0000010 : 7'bz;  // Controlled_Buffer controlled_buffer_1
  assign Adr = RTS ? 7'b0000011 : 7'bz;  // Controlled_Buffer controlled_buffer_2
  assign Adr = RTI ? 7'b0001001 : 7'bz;  // Controlled_Buffer controlled_buffer_3
  assign Adr = ROTR ? 7'b0011000 : 7'bz;  // Controlled_Buffer controlled_buffer_4
  assign Adr = ROTRC ? 7'b0011001 : 7'bz;  // Controlled_Buffer controlled_buffer_5
  assign Adr = PUSH ? 7'b0011010 : 7'bz;  // Controlled_Buffer controlled_buffer_6
  assign Adr = POP ? 7'b0100000 : 7'bz;  // Controlled_Buffer controlled_buffer_7
  assign Adr = BLEQ ? 7'b0101000 : 7'bz;  // Controlled_Buffer controlled_buffer_8
  assign Adr = BGREU ? 7'b0101010 : 7'bz;  // Controlled_Buffer controlled_buffer_9
  assign Adr = BNNG ? 7'b0101100 : 7'bz;  // Controlled_Buffer controlled_buffer_10
  assign Adr = BGRT ? 7'b0101110 : 7'bz;  // Controlled_Buffer controlled_buffer_11
  assign Adr = JLEQ ? 7'b0110000 : 7'bz;  // Controlled_Buffer controlled_buffer_12
  assign Adr = JSR ? 7'b0110011 : 7'bz;  // Controlled_Buffer controlled_buffer_13
  assign Adr = JMP ? 7'b0110010 : 7'bz;  // Controlled_Buffer controlled_buffer_14
  assign Adr = LD ? 7'b0111010 : 7'bz;  // Controlled_Buffer controlled_buffer_15
  assign Adr = ST ? 7'b1000000 : 7'bz;  // Controlled_Buffer controlled_buffer_16
  assign Adr = ADD ? 7'b0111100 : 7'bz;  // Controlled_Buffer controlled_buffer_17
  assign Adr = INC ? 7'b1000111 : 7'bz;  // Controlled_Buffer controlled_buffer_18
  assign Adr = LOR ? 7'b0111110 : 7'bz;  // Controlled_Buffer controlled_buffer_19
  assign Adr = STRFIND ? 7'b1001110 : 7'bz;  // Controlled_Buffer controlled_buffer_20
endmodule

module GPR16x16 (
  input  [15:0] DI,
  input  [3:0] A,
  input  WR,
  input  CLK,
  input  rst,
  input  inc,
  output [15:0] DO
);

  wire and_1_out, and_2_out, and_3_out, and_4_out, and_5_out, and_6_out, and_7_out, and_8_out, and_9_out,
       and_10_out, and_11_out, and_12_out, and_13_out, and_14_out, and_15_out, and_16_out, and_17_out,
       and_18_out, and_19_out, and_20_out, and_21_out, and_22_out, and_23_out, and_24_out, and_25_out,
       and_26_out, and_27_out, and_28_out, and_29_out, and_30_out, and_31_out, and_32_out, CS0, CS1, CS2,
       CS3, CS4, CS5, CS6, CS7, CS8, CS9, CS10, CS11, CS12, CS13, CS14, CS15;
  wire [15:0] counter_1_q, counter_2_q, counter_3_q, counter_4_q, counter_5_q, counter_6_q, counter_7_q,
       counter_8_q, counter_9_q, counter_10_q, counter_11_q, counter_12_q, counter_13_q, counter_14_q,
       counter_15_q, counter_16_q;

  Decoder #(.enable("false"), .select(4)) decoder_1 (
    .out0(CS0), .out1(CS1), .out2(CS2), .out3(CS3), .out4(CS4), .out5(CS5), .out6(CS6), .out7(CS7),
    .out8(CS8), .out9(CS9), .out10(CS10), .out11(CS11), .out12(CS12), .out13(CS13), .out14(CS14),
    .out15(CS15), .sel(A));
  and and_1 (and_1_out, CS0, inc);
  and and_2 (and_2_out, CS4, inc);
  and and_3 (and_3_out, CS8, inc);
  and and_4 (and_4_out, CS12, inc);
  Counter #(.max('hffff), .width(16)) counter_1 (
    .clr(rst), .load(and_5_out), .up(1'b1), .count(and_1_out), .clk(CLK), .D(DI), .Q(counter_1_q));  // open: carry
  and and_5 (and_5_out, CS0, WR);
  Counter #(.max('hffff), .width(16)) counter_2 (
    .clr(rst), .load(and_6_out), .up(1'b1), .count(and_2_out), .clk(CLK), .D(DI), .Q(counter_2_q));  // open: carry
  and and_6 (and_6_out, CS4, WR);
  Counter #(.max('hffff), .width(16)) counter_3 (
    .clr(rst), .load(and_7_out), .up(1'b1), .count(and_3_out), .clk(CLK), .D(DI), .Q(counter_3_q));  // open: carry
  and and_7 (and_7_out, CS8, WR);
  Counter #(.max('hffff), .width(16)) counter_4 (
    .clr(rst), .load(and_8_out), .up(1'b1), .count(and_4_out), .clk(CLK), .D(DI), .Q(counter_4_q));  // open: carry
  and and_8 (and_8_out, CS12, WR);
  assign DO = CS0 ? counter_1_q : 16'bz;  // Controlled_Buffer controlled_buffer_1
  assign DO = CS4 ? counter_2_q : 16'bz;  // Controlled_Buffer controlled_buffer_2
  assign DO = CS8 ? counter_3_q : 16'bz;  // Controlled_Buffer controlled_buffer_3
  assign DO = CS12 ? counter_4_q : 16'bz;  // Controlled_Buffer controlled_buffer_4
  and and_9 (and_9_out, CS5, inc);
  and and_10 (and_10_out, CS9, inc);
  and and_11 (and_11_out, CS13, inc);
  and and_12 (and_12_out, CS1, inc);
  and and_13 (and_13_out, CS5, WR);
  and and_14 (and_14_out, CS9, WR);
  and and_15 (and_15_out, CS13, WR);
  Counter #(.max('hffff), .width(16)) counter_5 (
    .clr(rst), .load(and_16_out), .up(1'b1), .count(and_12_out), .clk(CLK), .D(DI), .Q(counter_5_q));  // open: carry
  and and_16 (and_16_out, CS1, WR);
  Counter #(.max('hffff), .width(16)) counter_6 (
    .clr(rst), .load(and_13_out), .up(1'b1), .count(and_9_out), .clk(CLK), .D(DI), .Q(counter_6_q));  // open: carry
  Counter #(.max('hffff), .width(16)) counter_7 (
    .clr(rst), .load(and_14_out), .up(1'b1), .count(and_10_out), .clk(CLK), .D(DI), .Q(counter_7_q));  // open: carry
  Counter #(.max('hffff), .width(16)) counter_8 (
    .clr(rst), .load(and_15_out), .up(1'b1), .count(and_11_out), .clk(CLK), .D(DI), .Q(counter_8_q));  // open: carry
  assign DO = CS1 ? counter_5_q : 16'bz;  // Controlled_Buffer controlled_buffer_5
  assign DO = CS5 ? counter_6_q : 16'bz;  // Controlled_Buffer controlled_buffer_6
  assign DO = CS9 ? counter_7_q : 16'bz;  // Controlled_Buffer controlled_buffer_7
  assign DO = CS13 ? counter_8_q : 16'bz;  // Controlled_Buffer controlled_buffer_8
  and and_17 (and_17_out, CS2, inc);
  and and_18 (and_18_out, CS6, inc);
  and and_19 (and_19_out, CS10, inc);
  and and_20 (and_20_out, CS14, inc);
  Counter #(.max('hffff), .width(16)) counter_9 (
    .clr(rst), .load(and_21_out), .up(1'b1), .count(and_17_out), .clk(CLK), .D(DI), .Q(counter_9_q));  // open: carry
  and and_21 (and_21_out, CS2, WR);
  Counter #(.max('hffff), .width(16)) counter_10 (
    .clr(rst), .load(and_22_out), .up(1'b1), .count(and_18_out), .clk(CLK), .D(DI), .Q(counter_10_q));  // open: carry
  and and_22 (and_22_out, CS6, WR);
  Counter #(.max('hffff), .width(16)) counter_11 (
    .clr(rst), .load(and_23_out), .up(1'b1), .count(and_19_out), .clk(CLK), .D(DI), .Q(counter_11_q));  // open: carry
  and and_23 (and_23_out, CS10, WR);
  Counter #(.max('hffff), .width(16)) counter_12 (
    .clr(rst), .load(and_24_out), .up(1'b1), .count(and_20_out), .clk(CLK), .D(DI), .Q(counter_12_q));  // open: carry
  and and_24 (and_24_out, CS14, WR);
  assign DO = CS2 ? counter_9_q : 16'bz;  // Controlled_Buffer controlled_buffer_9
  assign DO = CS6 ? counter_10_q : 16'bz;  // Controlled_Buffer controlled_buffer_10
  assign DO = CS10 ? counter_11_q : 16'bz;  // Controlled_Buffer controlled_buffer_11
  assign DO = CS14 ? counter_12_q : 16'bz;  // Controlled_Buffer controlled_buffer_12
  and and_25 (and_25_out, CS7, inc);
  and and_26 (and_26_out, CS11, inc);
  and and_27 (and_27_out, CS15, inc);
  and and_28 (and_28_out, CS3, inc);
  and and_29 (and_29_out, CS7, WR);
  and and_30 (and_30_out, CS11, WR);
  and and_31 (and_31_out, CS15, WR);
  Counter #(.max('hffff), .width(16)) counter_13 (
    .clr(rst), .load(and_32_out), .up(1'b1), .count(and_28_out), .clk(CLK), .D(DI), .Q(counter_13_q));  // open: carry
  and and_32 (and_32_out, CS3, WR);
  Counter #(.max('hffff), .width(16)) counter_14 (
    .clr(rst), .load(and_29_out), .up(1'b1), .count(and_25_out), .clk(CLK), .D(DI), .Q(counter_14_q));  // open: carry
  Counter #(.max('hffff), .width(16)) counter_15 (
    .clr(rst), .load(and_30_out), .up(1'b1), .count(and_26_out), .clk(CLK), .D(DI), .Q(counter_15_q));  // open: carry
  Counter #(.max('hffff), .width(16)) counter_16 (
    .clr(rst), .load(and_31_out), .up(1'b1), .count(and_27_out), .clk(CLK), .D(DI), .Q(counter_16_q));  // open: carry
  assign DO = CS3 ? counter_13_q : 16'bz;  // Controlled_Buffer controlled_buffer_13
  assign DO = CS7 ? counter_14_q : 16'bz;  // Controlled_Buffer controlled_buffer_14
  assign DO = CS11 ? counter_15_q : 16'bz;  // Controlled_Buffer controlled_buffer_15
  assign DO = CS15 ? counter_16_q : 16'bz;  // Controlled_Buffer controlled_buffer_16

  // Other names for the same wires on the sheet: incREG = inc; inREG[15:0] = DI; outREG[15:0] = DO
endmodule

module INTERRUPT_INTERFACE_4 (
  input  BTN_INTR0,
  input  BTN_INTR1,
  input  BTN_INTR2,
  input  BTN_INTR3,
  input  inta,
  input  [1:0] UEXT,
  input  CLK,
  output [3:0] intr
);

  wire and_1_out, and_2_out, and_3_out, and_4_out, D0, D1, D2, D3;

  Decoder #(.select(2)) decoder_1 (.out0(D0), .out1(D1), .out2(D2), .out3(D3), .sel(UEXT), .en(inta));
  and and_1 (and_1_out, D0, ~BTN_INTR0);  // AND_Gate
  and and_2 (and_2_out, D1, ~BTN_INTR1);  // AND_Gate
  and and_3 (and_3_out, D2, ~BTN_INTR2);  // AND_Gate
  and and_4 (and_4_out, D3, ~BTN_INTR3);  // AND_Gate
  S_R_Flip_Flop s_r_ff_1 (.S(BTN_INTR0), .R(and_1_out), .clk(CLK), .Q(intr[0]));  // open: reset, Qn, preset
  S_R_Flip_Flop s_r_ff_2 (.S(BTN_INTR1), .R(and_2_out), .clk(CLK), .Q(intr[1]));  // open: reset, Qn, preset
  S_R_Flip_Flop s_r_ff_3 (.S(BTN_INTR2), .R(and_3_out), .clk(CLK), .Q(intr[2]));  // open: reset, Qn, preset
  S_R_Flip_Flop s_r_ff_4 (.S(BTN_INTR3), .R(and_4_out), .clk(CLK), .Q(intr[3]));  // open: reset, Qn, preset
endmodule

module RisingEdge (
  input  INPUT,
  input  CLK,
  output OUTPUT
);

  wire d_ff_1_q, d_ff_2_q;

  D_Flip_Flop d_ff_1 (.D(INPUT), .clk(CLK), .Q(d_ff_1_q));  // open: Qn, preset, reset
  D_Flip_Flop d_ff_2 (.D(d_ff_1_q), .clk(CLK), .Q(d_ff_2_q));  // open: Qn, preset, reset
  and and_1 (OUTPUT, d_ff_1_q, ~d_ff_2_q);  // AND_Gate
endmodule
