// Logisim project ORT2Project.circ as structural Verilog: 8 circuits, main circuit COMPUTER
module COMPUTER (
  input  DEBUG
);

  wire BTN_RST_out, CLK, cpu_1_inta, interrupt_interface_4_1_p4, interrupt_interface_4_1_p5,
       interrupt_interface_4_1_p6, interrupt_interface_4_1_p7, pull_resistor_4_node, pull_resistor_5_node,
       ram_1_fcbus, rst;
  wire [1:0] cpu_1_uext;
  wire [3:0] interrupt_interface_4_1_p1;
  wire [7:0] pull_resistor_3_node, risingedge_1_p5;
  wire [15:0] risingedge_1_p4;

  Button BTN_RST (.out(BTN_RST_out));
  Clock u_CLK (.out(CLK));
  // RisingEdge risingedge_1: pin names not known; wires that end beside it: BTN_RST_out, CLK, rst, risingedge_1_p4, risingedge_1_p5
  RAM ram_1 (
    .DOUT(risingedge_1_p5), .FCBUS(ram_1_fcbus), .CLK(CLK), .DIN(pull_resistor_3_node),
    .WRMEM(pull_resistor_4_node), .RDMEM(pull_resistor_5_node), .rst(rst), .DEBUG(DEBUG),
    .ADR(risingedge_1_p4));
  Pull_Resistor pull_resistor_1 (.node(risingedge_1_p4));
  Pull_Resistor pull_resistor_2 (.node(risingedge_1_p5));
  Pull_Resistor pull_resistor_3 (.node(pull_resistor_3_node));
  Pull_Resistor pull_resistor_4 (.node(pull_resistor_4_node));
  Pull_Resistor pull_resistor_5 (.node(pull_resistor_5_node));
  Pull_Resistor pull_resistor_6 (.node(ram_1_fcbus));
  CPU cpu_1 (
    .out_8(pull_resistor_4_node), .out_9(pull_resistor_5_node), .inta(cpu_1_inta), .UEXT(cpu_1_uext),
    .ABUS(risingedge_1_p4), .DOUTBUS(pull_resistor_3_node), .in_3(ram_1_fcbus), .in_1(rst), .in_2(CLK),
    .DIN(risingedge_1_p5), .intr3_0(interrupt_interface_4_1_p1));
  // INTERRUPT_INTERFACE_4 interrupt_interface_4_1: pin names not known; wires that end beside it: interrupt_interface_4_1_p1, cpu_1_inta, cpu_1_uext, interrupt_interface_4_1_p4, interrupt_interface_4_1_p5, interrupt_interface_4_1_p6, interrupt_interface_4_1_p7, CLK
  Button BTN_INTR3 (.out(interrupt_interface_4_1_p4));
  Button BTN_INTR2 (.out(interrupt_interface_4_1_p5));
  Button BTN_INTR1 (.out(interrupt_interface_4_1_p6));
  Button BTN_INTR0 (.out(interrupt_interface_4_1_p7));
endmodule

module CPU (
  input  in_1,
  input  in_2,
  input  in_3,
  input  [7:0] DIN,
  input  [3:0] intr3_0,
  output [15:0] ABUS,
  output [7:0] DOUTBUS,
  output out_8,
  output out_9,
  output inta,
  output [1:0] UEXT
);

  wire [3:0] common_1_phaseffbus;
  wire [7:0] common_1_addrbus, pull_resistor_5_node;
  wire [11:0] pull_resistor_6_node;
  wire [15:0] A, ALU, B, INTRADDR, PSW;
  wire [20:0] common_1_instrucbus;
  wire [31:0] pull_resistor_4_node;

  COMMON common_1 (
    .MAR(ABUS), .MDR(DOUTBUS), .PHASEFFBUS(common_1_phaseffbus), .ADDRBUS(common_1_addrbus), .PSW(PSW),
    .B(B), .INSTRUCBUS(common_1_instrucbus), .CBUS(pull_resistor_4_node), .CFFBUS(pull_resistor_5_node),
    .CPSW(pull_resistor_6_node), .CLK(in_2), .RST(in_1), .DIN(DIN), .IVTPPDSP(INTRADDR), .A(A), .ALU(ALU));
  Pull_Resistor pull_resistor_1 (.node(common_1_phaseffbus));
  Pull_Resistor pull_resistor_2 (.node(common_1_instrucbus));
  Pull_Resistor pull_resistor_3 (.node(common_1_addrbus));
  Pull_Resistor pull_resistor_4 (.node(pull_resistor_4_node));
  Pull_Resistor pull_resistor_5 (.node(pull_resistor_5_node));
  Pull_Resistor pull_resistor_6 (.node(pull_resistor_6_node));
  FETCH fetch_1 (
    .rdMEM(out_9), .CFFBUS(pull_resistor_5_node), .CBUS(pull_resistor_4_node), .in_2(in_2), .in_3(in_3),
    .in_1(in_1), .PSW(PSW), .INSTRUCBUS(common_1_instrucbus), .ADDRBUS(common_1_addrbus),
    .PHASEFFBUS(common_1_phaseffbus));
  ADDR addr_1 (
    .CBUS(pull_resistor_4_node), .rdMEM(out_9), .CFFBUS(pull_resistor_5_node), .in_2(in_2), .in_3(in_3),
    .in_1(in_1), .PHASEFFBUS(common_1_phaseffbus), .INSTRUCBUS(common_1_instrucbus),
    .ADDRBUS(common_1_addrbus));
  EXEC exec_1 (
    .rdMEM(out_9), .wrMEM(out_8), .CBUS(pull_resistor_4_node), .A(A), .ALU(ALU),
    .CFFBUS(pull_resistor_5_node), .CPSW(pull_resistor_6_node), .PSW(PSW), .MDR(DOUTBUS),
    .INSTRUCBUS(common_1_instrucbus), .ADDRBUS(common_1_addrbus), .PHASEFFBUS(common_1_phaseffbus), .B(B),
    .in_1(in_1), .in_2(in_2), .in_3(in_3));
  INTR intr_1 (
    .wrMEM(out_8), .rdMEM(out_9), .UEXT(UEXT), .inta(inta), .ADDIVTP(INTRADDR),
    .CFFBUS(pull_resistor_5_node), .CBUS(pull_resistor_4_node), .rst(in_1), .CLK(in_2), .FCBUS(in_3),
    .PSW(PSW), .intr3_0(intr3_0), .PHASEFFBUS(common_1_phaseffbus), .INSTRUCBUS(common_1_instrucbus));

  // Other names for the same wires on the sheet: CLK = in_2; FCBUS = in_3; MAR[15:0] = ABUS; MDR[7:0] = DOUTBUS;
  //   RD = out_9; rst = in_1; WR = out_8
endmodule

module COMMON (
  input  CLK,
  input  RST,
  input  [7:0] DIN,
  input  [15:0] IVTPPDSP,
  input  [15:0] A,
  input  [15:0] ALU,
  input  [31:0] CBUS,
  input  [7:0] CFFBUS,
  input  [11:0] CPSW,
  output [15:0] MAR,
  output [7:0] MDR,
  output [3:0] PHASEFFBUS,
  output [7:0] ADDRBUS,
  output [15:0] PSW,
  output [15:0] B,
  output [20:0] INSTRUCBUS
);

  wire adr, and_2_out, and_3_out, and_7_out, and_8_out, and_9_out, and_10_out, and_11_out, and_12_out,
       and_13_out, and_14_out, and_15_out, and_16_out, bezadr, branch3, C, decoder_2_out5, decoder_2_out6,
       decoder_2_out7, decoder_3_out6, decoder_3_out7, decoder_5_out7, I, invalid_group, invalid_instr1,
       invalid_instr2, invalid_instr3, invalid_instr4, jmp3, N, not_1_out, or_2_out, or_6_out, or_7_out,
       or_8_out, or_9_out, or_10_out, or_11_out, or_12_out, or_13_out, V, Z;
  wire [2:0] instr;
  wire [3:0] multiplexer_4_out;
  wire [7:0] IR7_0, IR15_8, IR23_16, multiplexer_2_out;
  wire [7:3] IR31_24;
  wire [15:0] adder_1_out, adder_2_out, adder_3_out, bit_extender_1_out, GPR, multiplexer_1_out,
       multiplexer_3_out, multiplexer_5_out, multiplexer_6_out, PC, SP, subtractor_1_out;

  assign N = CPSW[8] ? 1'b1 : 1'bz;  // Controlled_Buffer controlled_buffer_1
  assign V = CPSW[9] ? 1'b1 : 1'bz;  // Controlled_Buffer controlled_buffer_2
  assign C = CPSW[10] ? 1'b1 : 1'bz;  // Controlled_Buffer controlled_buffer_3
  assign I = CPSW[11] ? 1'b1 : 1'bz;  // Controlled_Buffer controlled_buffer_4
  assign Z = CPSW[7] ? 1'b1 : 1'bz;  // Controlled_Buffer controlled_buffer_5
  Register register_1 (.D(MDR), .en(CBUS[8]), .clk(CLK), .Q({IR31_24, instr}));  // open: clr
  Register register_2 (.D(MDR), .en(CBUS[6]), .clk(CLK), .Q(IR15_8));  // open: clr
  or or_1 (invalid_group, IR31_24[6], IR31_24[3], IR31_24[7]);
  Multiplexer #(.enable("false"), .select(3), .width(16)) multiplexer_1 (
    .in0(PC), .in1({IR15_8, IR7_0}), .in2({B[15:8], MDR}), .in4(GPR), .in5(SP), .in6(IVTPPDSP), .in7(A),
    .out(multiplexer_1_out), .sel(CBUS[18:16]));  // open: in3
  Decoder #(.enable("false"), .select(2)) decoder_1 (
    .out0(bezadr), .out1(branch3), .out2(jmp3), .out3(adr), .sel(IR31_24[5:4]));
  Decoder #(.select(3)) decoder_2 (
    .out0(INSTRUCBUS[7]), .out1(INSTRUCBUS[8]), .out2(INSTRUCBUS[9]), .out3(INSTRUCBUS[10]),
    .out4(INSTRUCBUS[11]), .out5(decoder_2_out5), .out6(decoder_2_out6), .out7(decoder_2_out7), .sel(instr),
    .en(branch3));
  Decoder #(.select(3)) decoder_3 (
    .out0(INSTRUCBUS[14]), .out1(INSTRUCBUS[15]), .out2(INSTRUCBUS[16]), .out3(INSTRUCBUS[17]),
    .out4(INSTRUCBUS[18]), .out5(INSTRUCBUS[19]), .out6(decoder_3_out6), .out7(decoder_3_out7), .sel(instr),
    .en(adr));
  Adder #(.width(16)) adder_1 (.a(B), .b(16'h1), .out(adder_1_out));  // open: cin, cout
  or or_2 (or_2_out, CBUS[0], CBUS[1]);
  or or_3 (invalid_instr1, decoder_2_out7, decoder_2_out6, decoder_2_out5);
  or or_4 (invalid_instr3, decoder_3_out7, decoder_3_out6);
  or or_5 (INSTRUCBUS[20], invalid_group, invalid_instr1, invalid_instr2, invalid_instr3, invalid_instr4);
  Multiplexer #(.enable("false"), .select(4), .width(8)) multiplexer_2 (
    .in0(DIN), .in1(PC[15:8]), .in2(PC[7:0]), .in3(PSW[15:8]), .in4(PSW[7:0]), .in5(A[15:8]), .in6(A[7:0]),
    .in7(adder_1_out[15:8]), .in8(adder_1_out[7:0]), .out(multiplexer_2_out), .sel({CBUS[28], CBUS[25:23]}));  // open: in9, in10, in11, in12, in13, in14, in15
  Counter #(.max('hffff), .width(16)) counter_1 (
    .clr(RST), .load(CBUS[0]), .up(1'b1), .count(or_2_out), .clk(CLK), .D(multiplexer_1_out), .Q(MAR));  // open: carry
  Register register_3 (.D(MDR), .en(CBUS[7]), .clk(CLK), .Q(IR23_16));  // open: clr
  Register register_4 (.D(MDR), .en(CBUS[5]), .clk(CLK), .Q(IR7_0));  // open: clr
  Register register_5 (.D(multiplexer_2_out), .en(CBUS[2]), .clk(CLK), .Q(MDR));  // open: clr
  Decoder #(.select(3)) decoder_4 (
    .out0(INSTRUCBUS[0]), .out1(INSTRUCBUS[1]), .out2(INSTRUCBUS[2]), .out3(INSTRUCBUS[3]),
    .out4(INSTRUCBUS[4]), .out5(INSTRUCBUS[5]), .out6(INSTRUCBUS[6]), .out7(invalid_instr4), .sel(instr),
    .en(bezadr));
  or or_6 (or_6_out, instr[2], instr[1]);
  Decoder #(.select(3)) decoder_5 (
    .out0(ADDRBUS[0]), .out1(ADDRBUS[1]), .out2(ADDRBUS[2]), .out3(ADDRBUS[3]), .out4(ADDRBUS[4]),
    .out5(ADDRBUS[5]), .out6(ADDRBUS[6]), .out7(decoder_5_out7), .sel(IR23_16[6:4]), .en(adr));
  or or_7 (or_7_out, IR23_16[7], decoder_5_out7, and_2_out, and_3_out);
  and and_1 (ADDRBUS[7], adr, or_7_out);
  or or_8 (or_8_out, IR23_16[0], IR23_16[1], IR23_16[2], IR23_16[3]);
  or or_9 (or_9_out, ADDRBUS[0], ADDRBUS[1], ADDRBUS[2]);
  not not_1 (not_1_out, instr[0]);
  and and_2 (and_2_out, ADDRBUS[0], or_10_out);
  and and_3 (and_3_out, or_8_out, or_9_out);
  and and_4 (INSTRUCBUS[12], instr[0], jmp3);
  and and_5 (INSTRUCBUS[13], not_1_out, jmp3);
  and and_6 (invalid_instr2, jmp3, or_6_out);
  or or_10 (or_10_out, INSTRUCBUS[15], INSTRUCBUS[17]);
  S_R_Flip_Flop s_r_ff_1 (.S(CFFBUS[0]), .R(CFFBUS[1]), .clk(CLK), .Q(PHASEFFBUS[0]), .preset(RST));  // open: reset, Qn
  S_R_Flip_Flop s_r_ff_2 (.S(CFFBUS[2]), .R(CFFBUS[3]), .clk(CLK), .Q(PHASEFFBUS[1]), .reset(RST));  // open: Qn, preset
  or or_11 (or_11_out, CBUS[3], RST);
  Adder #(.width(16)) adder_2 (.a(PC), .b(bit_extender_1_out), .out(adder_2_out));  // open: cin, cout
  assign bit_extender_1_out = {{8{IR23_16[7]}}, IR23_16};  // Bit_Extender bit_extender_1
  Counter #(.max('hffff), .width(16)) counter_2 (
    .load(or_11_out), .up(1'b1), .count(or_12_out), .clk(CLK), .D(multiplexer_3_out), .Q(PC));  // open: clr, carry
  or or_12 (or_12_out, or_11_out, CBUS[4]);
  Multiplexer #(.enable("false"), .select(3), .width(16)) multiplexer_3 (
    .in0(16'h1000), .in1({MDR, PC[7:0]}), .in2({PC[15:8], MDR}), .in3(adder_2_out), .in4({IR23_16, IR15_8}),
    .out(multiplexer_3_out), .sel(CBUS[15:13]));  // open: in5, in6, in7
  S_R_Flip_Flop s_r_ff_3 (.S(CFFBUS[4]), .R(CFFBUS[5]), .clk(CLK), .Q(PHASEFFBUS[2]), .reset(RST));  // open: Qn, preset
  S_R_Flip_Flop s_r_ff_4 (.S(CFFBUS[6]), .R(CFFBUS[7]), .clk(CLK), .Q(PHASEFFBUS[3]), .reset(RST));  // open: Qn, preset
  Pull_Resistor pull_resistor_1 (.node(N));
  Pull_Resistor pull_resistor_2 (.node(C));
  S_R_Flip_Flop s_r_ff_5 (.S(CPSW[0]), .R(CPSW[1]), .clk(CLK), .Q(PSW[0]), .preset(RST));  // open: reset, Qn
  and and_7 (and_7_out, CPSW[3], N);
  S_R_Flip_Flop s_r_ff_6 (.S(and_7_out), .R(and_8_out), .clk(CLK), .Q(PSW[2]), .reset(RST));  // open: Qn, preset
  and and_8 (and_8_out, CPSW[3], ~N);  // AND_Gate
  and and_9 (and_9_out, CPSW[5], C);
  S_R_Flip_Flop s_r_ff_7 (.S(and_9_out), .R(and_10_out), .clk(CLK), .Q(PSW[4]), .reset(RST));  // open: Qn, preset
  and and_10 (and_10_out, CPSW[5], ~C);  // AND_Gate
  assign Z = CBUS[26] ? MDR[1] : 1'bz;  // Controlled_Buffer controlled_buffer_6
  Counter #(.max('hffff), .width(16)) counter_3 (
    .load(RST), .up(CBUS[11]), .count(or_13_out), .clk(CLK), .D(16'hf000), .Q(SP));  // open: clr, carry
  or or_13 (or_13_out, RST, CBUS[11], CBUS[12]);
  assign N = CBUS[26] ? MDR[2] : 1'bz;  // Controlled_Buffer controlled_buffer_7
  assign V = CBUS[26] ? MDR[3] : 1'bz;  // Controlled_Buffer controlled_buffer_8
  assign C = CBUS[26] ? MDR[4] : 1'bz;  // Controlled_Buffer controlled_buffer_9
  assign I = CBUS[26] ? MDR[7] : 1'bz;  // Controlled_Buffer controlled_buffer_10
  Adder #(.width(16)) adder_3 (.a(GPR), .b(16'h2), .out(adder_3_out));  // open: cin, cout
  Subtractor #(.width(16)) subtractor_1 (.a(GPR), .b(16'h2), .out(subtractor_1_out));  // open: bin, bout
  Multiplexer #(.enable("false"), .width(4)) multiplexer_4 (
    .in0(IR23_16[3:0]), .out(multiplexer_4_out), .sel(CBUS[19]));  // open: in1
  Pull_Resistor pull_resistor_3 (.node(V));
  Pull_Resistor pull_resistor_4 (.node(Z));
  Pull_Resistor pull_resistor_5 (.node(I));
  and and_11 (and_11_out, CPSW[4], V);
  S_R_Flip_Flop s_r_ff_8 (.S(and_11_out), .R(and_12_out), .clk(CLK), .Q(PSW[3]), .reset(RST));  // open: Qn, preset
  and and_12 (and_12_out, CPSW[4], ~V);  // AND_Gate
  and and_13 (and_13_out, CPSW[2], Z);
  S_R_Flip_Flop s_r_ff_9 (.S(and_13_out), .R(and_14_out), .clk(CLK), .Q(PSW[1]), .reset(RST));  // open: Qn, preset
  and and_14 (and_14_out, CPSW[2], ~Z);  // AND_Gate
  and and_15 (and_15_out, CPSW[6], I);
  S_R_Flip_Flop s_r_ff_10 (.S(and_15_out), .R(and_16_out), .clk(CLK), .Q(PSW[15]), .preset(RST));  // open: reset, Qn
  and and_16 (and_16_out, CPSW[6], ~I);  // AND_Gate
  Multiplexer #(.enable("false"), .select(2), .width(16)) multiplexer_5 (
    .in0(adder_3_out), .in1(subtractor_1_out), .in2(A), .out(multiplexer_5_out), .sel({CBUS[29], CBUS[20]}));  // open: in3
  GPR16x16 gpr16x16_1 (
    .DO(GPR), .WR(CBUS[10]), .CLK(CLK), .rst(RST), .inc(CBUS[27]), .DI(multiplexer_5_out),
    .A(multiplexer_4_out));
  Register #(.width(16)) register_6 (.D(multiplexer_6_out), .en(CBUS[9]), .clk(CLK), .Q(B));  // open: clr
  Multiplexer #(.enable("false"), .select(2), .width(16)) multiplexer_6 (
    .in0({IR15_8, IR7_0}), .in1({MDR, B[7:0]}), .in2({B[15:8], MDR}), .in3(GPR), .out(multiplexer_6_out),
    .sel(CBUS[22:21]));

  // Other names for the same wires on the sheet: mxMAR0 = CBUS[16]; mxMAR1 = CBUS[17]; mxMAR2 = CBUS[18];
  //   mxMDR0 = CBUS[23]; mxMDR1 = CBUS[24]; mxMDR2 = CBUS[25]; mxMDR3 = CBUS[28]; mxPC0 = CBUS[13]; mxPC1 = CBUS[14];
  //   mxPC2 = CBUS[15]; mxB0 = CBUS[21]; mxB1 = CBUS[22]; mxGPRIN0 = CBUS[20]; mxGPRIN1 = CBUS[29];
  //   immed = ADDRBUS[0]; memdir = ADDRBUS[1]; memind = ADDRBUS[2]; regind = ADDRBUS[3]; postincr = ADDRBUS[4];
  //   postdec = ADDRBUS[5]; regdir = ADDRBUS[6]; graddr = ADDRBUS[7]; ldMAR = CBUS[0]; incMAR = CBUS[1];
  //   ldMDR = CBUS[2]; ldPC = CBUS[3]; incPC = CBUS[4]; ldIR7_0 = CBUS[5]; ldIR15_8 = CBUS[6]; ldIR23_16 = CBUS[7];
  //   ldIR31_24 = CBUS[8]; ldB = CBUS[9]; wrGPR = CBUS[10]; incSP = CBUS[11]; decSP = CBUS[12]; mxGPRADR0 = CBUS[19];
  //   ldPSWMDR = CBUS[26]; incGPR = CBUS[27]; stFETCH = CFFBUS[0]; clFETCH = CFFBUS[1]; stADDR = CFFBUS[2];
  //   clADDR = CFFBUS[3]; stEXEC = CFFBUS[4]; clEXEC = CFFBUS[5]; stINTR = CFFBUS[6]; clINTR = CFFBUS[7];
  //   stPSWSTART = CPSW[0]; clPSWSTART = CPSW[1]; ldPSWZ = CPSW[2]; ldPSWN = CPSW[3]; ldPSWV = CPSW[4];
  //   ldPSWC = CPSW[5]; ldPSWI = CPSW[6]; ENTRADDR[15:0] = IVTPPDSP; HALT = INSTRUCBUS[0]; RTS = INSTRUCBUS[1];
  //   RTI = INSTRUCBUS[2]; ROTR = INSTRUCBUS[3]; ROTRC = INSTRUCBUS[4]; PUSH = INSTRUCBUS[5]; POP = INSTRUCBUS[6];
  //   BLEQ = INSTRUCBUS[7]; BGREU = INSTRUCBUS[8]; BNNG = INSTRUCBUS[9]; BGRT = INSTRUCBUS[10]; JLEQ = INSTRUCBUS[11];
  //   JSR = INSTRUCBUS[12]; JMP = INSTRUCBUS[13]; LD = INSTRUCBUS[14]; ST = INSTRUCBUS[15]; ADD = INSTRUCBUS[16];
  //   INC = INSTRUCBUS[17]; LOR = INSTRUCBUS[18]; STRFIND = INSTRUCBUS[19]; grinst = INSTRUCBUS[20];
  //   IR31_24[2:0] = instr; FETCH = PHASEFFBUS[0]; ADDR = PHASEFFBUS[1]; EXEC = PHASEFFBUS[2]; INTR = PHASEFFBUS[3];
  //   PSWSTART = PSW[0]; PSWZ = PSW[1]; PSWN = PSW[2]; PSWV = PSW[3]; PSWC = PSW[4]; PSWI = PSW[15]

  // Notes on the sheet:
  //   MAR
  //   MDR
  //   Instrukcijski registar
  //   Dekoderi za prepoznavanje instrukcije na osnovu sadržaja registra IR31..24
  //   PC
  //   Faze izvršavanja instrukcije
  //   Registarski fajl
  //   B
  //   Kutija za vaše snove
  //   Programska statusna reč (PSW)
  //   SP
endmodule

module FETCH (
  input  in_1,
  input  in_2,
  input  in_3,
  input  [3:0] PHASEFFBUS,
  input  [7:0] ADDRBUS,
  input  [15:0] PSW,
  input  [20:0] INSTRUCBUS,
  output [31:0] CBUS,
  output [7:0] CFFBUS,
  output rdMEM
);

  wire addr2, and_1_out, and_2_out, and_3_out, and_4_out, and_5_out, and_6_out, and_7_out, and_8_out, bezadr,
       braddr2, brbezadr, brcnd, brgraddr, brgrinst, brjmp2, brjmp3, brnotFCBUS, brnotpswSTARTandFETCH,
       bruncnd, clFETCH, incPC, jmp2, jmp3, ldIR7_0, ldIR15_8, ldIR23_16, ldIR31_24, ldMAR, ldMDR,
       nand_1_out, or_4_out, rdMEM_t, stADDR, stEXEC;
  wire [4:0] counter_1_q;
  wire [19:11] rom_1_data;

  ROM #(.addrWidth(5), .dataWidth(20)) rom_1 (
    .addr(counter_1_q),
    .data({rom_1_data, stEXEC, stADDR, clFETCH, ldIR7_0, ldIR15_8, ldIR23_16, ldIR31_24, ldMDR, rdMEM_t, ldMAR, incPC}));
  or or_1 (jmp2, INSTRUCBUS[7], INSTRUCBUS[8], INSTRUCBUS[9], INSTRUCBUS[10]);
  or or_2 (jmp3, INSTRUCBUS[11], INSTRUCBUS[12], INSTRUCBUS[13]);
  or or_3 (bezadr, INSTRUCBUS[0], INSTRUCBUS[1], INSTRUCBUS[2], INSTRUCBUS[3], INSTRUCBUS[4], INSTRUCBUS[5], INSTRUCBUS[6]);
  or or_4 (or_4_out, brcnd, bruncnd);
  // Probe on rom_1_data[19:15]
  Counter #(.max('h1f), .width(5)) counter_1 (
    .clr(in_1), .load(or_4_out), .up(1'b1), .clk(in_2), .D(rom_1_data[19:15]), .Q(counter_1_q));  // open: count, carry
  or or_5 (addr2, ADDRBUS[4], ADDRBUS[5], ADDRBUS[3], ADDRBUS[6], ADDRBUS[7]);
  Decoder #(.enable("false"), .select(4)) decoder_1 (
    .out1(bruncnd), .out2(brnotpswSTARTandFETCH), .out3(brnotFCBUS), .out4(brgrinst), .out5(brbezadr),
    .out6(brjmp2), .out7(brgraddr), .out8(braddr2), .out9(brjmp3), .sel(rom_1_data[14:11]));  // open: out0, out10, out11, out12, out13, out14, out15
  // Probe on rom_1_data[14:11]
  // Probe on counter_1_q
  and and_1 (and_1_out, INSTRUCBUS[20], brgrinst);
  and and_2 (and_2_out, ADDRBUS[7], brgraddr);
  and and_3 (and_3_out, bezadr, brbezadr);
  and and_4 (and_4_out, jmp2, brjmp2);
  and and_5 (and_5_out, addr2, braddr2);
  and and_6 (and_6_out, jmp3, brjmp3);
  nand nand_1 (nand_1_out, PSW[0], PHASEFFBUS[0]);
  and and_7 (and_7_out, nand_1_out, brnotpswSTARTandFETCH);
  and and_8 (and_8_out, ~in_3, brnotFCBUS);  // AND_Gate
  or or_6 (brcnd, and_7_out, and_8_out, and_1_out, and_2_out, and_3_out, and_4_out, and_5_out, and_6_out);
  assign CBUS[6] = ldIR15_8 ? 1'b1 : 1'bz;  // Controlled_Buffer controlled_buffer_1
  assign CBUS[7] = ldIR23_16 ? 1'b1 : 1'bz;  // Controlled_Buffer controlled_buffer_2
  assign CFFBUS[2] = stADDR ? 1'b1 : 1'bz;  // Controlled_Buffer controlled_buffer_3
  assign CFFBUS[4] = stEXEC ? 1'b1 : 1'bz;  // Controlled_Buffer controlled_buffer_4
  assign rdMEM = rdMEM_t ? 1'b1 : 1'bz;  // Controlled_Buffer controlled_buffer_5
  assign CBUS[5] = ldIR7_0 ? 1'b1 : 1'bz;  // Controlled_Buffer controlled_buffer_6
  assign CBUS[8] = ldIR31_24 ? 1'b1 : 1'bz;  // Controlled_Buffer controlled_buffer_7
  assign CFFBUS[1] = clFETCH ? 1'b1 : 1'bz;  // Controlled_Buffer controlled_buffer_8
  assign CBUS[2] = ldMDR ? 1'b1 : 1'bz;  // Controlled_Buffer controlled_buffer_9
  assign CBUS[0] = ldMAR ? 1'b1 : 1'bz;  // Controlled_Buffer controlled_buffer_10
  assign CBUS[4] = incPC ? 1'b1 : 1'bz;  // Controlled_Buffer controlled_buffer_11

  // Other names for the same wires on the sheet: immed = ADDRBUS[0]; memdir = ADDRBUS[1]; memind = ADDRBUS[2];
  //   regind = ADDRBUS[3]; postincr = ADDRBUS[4]; postdec = ADDRBUS[5]; regdir = ADDRBUS[6]; graddr = ADDRBUS[7];
  //   incMAR = CBUS[1]; ldPC = CBUS[3]; ldB = CBUS[9]; wrGPR = CBUS[10]; incSP = CBUS[11]; decSP = CBUS[12];
  //   mxPC0 = CBUS[13]; mxPC1 = CBUS[14]; mxPC2 = CBUS[15]; mxMAR0 = CBUS[16]; mxMAR1 = CBUS[17]; mxMAR2 = CBUS[18];
  //   mxGPRADR0 = CBUS[19]; mxGPRIN0 = CBUS[20]; mxB0 = CBUS[21]; mxB1 = CBUS[22]; stFETCH = CFFBUS[0];
  //   clADDR = CFFBUS[3]; clEXEC = CFFBUS[5]; stINTR = CFFBUS[6]; clINTR = CFFBUS[7]; CLK = in_2; FCBUS = in_3;
  //   HALT = INSTRUCBUS[0]; RTS = INSTRUCBUS[1]; RTI = INSTRUCBUS[2]; ROTR = INSTRUCBUS[3]; ROTRC = INSTRUCBUS[4];
  //   PUSH = INSTRUCBUS[5]; POP = INSTRUCBUS[6]; BLEQ = INSTRUCBUS[7]; BGREU = INSTRUCBUS[8]; BNNG = INSTRUCBUS[9];
  //   BGRT = INSTRUCBUS[10]; JLEQ = INSTRUCBUS[11]; JSR = INSTRUCBUS[12]; JMP = INSTRUCBUS[13]; LD = INSTRUCBUS[14];
  //   ST = INSTRUCBUS[15]; ADD = INSTRUCBUS[16]; INC = INSTRUCBUS[17]; LOR = INSTRUCBUS[18]; STRFIND = INSTRUCBUS[19];
  //   grinst = INSTRUCBUS[20]; FETCH = PHASEFFBUS[0]; ADDR = PHASEFFBUS[1]; EXEC = PHASEFFBUS[2];
  //   INTR = PHASEFFBUS[3]; pswSTART = PSW[0]; rst = in_1

  // Notes on the sheet:
  //   contents of rom_1 (hex, n*v repeats v):
  //   1000 3 1180c 10 2000 92800 3 3980c 93020 3800 8c000 3 6180c 94840 3 7980c 80 b00 d00
  //   Operaciona jedinica
  //   Kontrolna jedinica
endmodule

module ADDR (
  input  in_1,
  input  in_2,
  input  in_3,
  input  [3:0] PHASEFFBUS,
  input  [7:0] ADDRBUS,
  input  [20:0] INSTRUCBUS,
  output [31:0] CBUS,
  output rdMEM,
  output [7:0] CFFBUS
);

  wire and_1_out, and_2_out, and_3_out, and_4_out, brcnd, brmul, brnotADDR, brnotFCBUS, brST, brSTorINC,
       bruncnd, clADDR, incMAR, ldB, ldMAR, ldMDR, mxB0, mxB1, mxGPRIN0, mxMAR0, mxMAR1, mxMAR2, or_1_out,
       rdMEM_t, stEXEC, wrGPR;
  wire [4:0] counter_1_q, kmadr_1_adr, multiplexer_1_out;
  wire [21:14] rom_1_data;

  ROM #(.addrWidth(5), .dataWidth(22)) rom_1 (
    .addr(counter_1_q),
    .data({rom_1_data, stEXEC, clADDR, mxB1, mxGPRIN0, wrGPR, mxMAR2, mxMAR1, mxB0, incMAR, ldMDR, rdMEM_t, mxMAR0, ldMAR, ldB}));
  Counter #(.max('h1f), .width(5)) counter_1 (
    .clr(in_1), .load(brcnd), .up(1'b1), .clk(in_2), .D(multiplexer_1_out), .Q(counter_1_q));  // open: count, carry
  Multiplexer #(.enable("false"), .width(5)) multiplexer_1 (
    .in0(rom_1_data[21:17]), .in1(kmadr_1_adr), .out(multiplexer_1_out), .sel(brmul));
  Decoder #(.enable("false"), .select(3)) decoder_1 (
    .out1(bruncnd), .out2(brnotADDR), .out3(brmul), .out4(brnotFCBUS), .out5(brST), .out6(brSTorINC),
    .sel(rom_1_data[16:14]));  // open: out0, out7
  KMADR kmadr_1 (
    .Adr(kmadr_1_adr), .memdir(ADDRBUS[1]), .memind(ADDRBUS[2]), .regind(ADDRBUS[3]), .postincr(ADDRBUS[4]),
    .postdec(ADDRBUS[5]), .regdir(ADDRBUS[6]), .immed(ADDRBUS[0]));
  or or_1 (or_1_out, INSTRUCBUS[15], INSTRUCBUS[17]);
  and and_1 (and_1_out, brnotADDR, ~PHASEFFBUS[1]);  // AND_Gate
  and and_2 (and_2_out, brSTorINC, or_1_out);
  and and_3 (and_3_out, brnotFCBUS, ~in_3);  // AND_Gate
  and and_4 (and_4_out, brST, INSTRUCBUS[15]);
  or or_2 (brcnd, bruncnd, brmul, and_1_out, and_2_out, and_3_out, and_4_out);
  assign CBUS[2] = ldMDR ? 1'b1 : 1'bz;  // Controlled_Buffer controlled_buffer_1
  assign CBUS[1] = incMAR ? 1'b1 : 1'bz;  // Controlled_Buffer controlled_buffer_2
  assign CBUS[9] = ldB ? 1'b1 : 1'bz;  // Controlled_Buffer controlled_buffer_3
  assign CBUS[10] = wrGPR ? 1'b1 : 1'bz;  // Controlled_Buffer controlled_buffer_4
  assign CBUS[16] = mxMAR0 ? 1'b1 : 1'bz;  // Controlled_Buffer controlled_buffer_5
  assign CBUS[17] = mxMAR1 ? 1'b1 : 1'bz;  // Controlled_Buffer controlled_buffer_6
  assign CBUS[18] = mxMAR2 ? 1'b1 : 1'bz;  // Controlled_Buffer controlled_buffer_7
  assign CBUS[20] = mxGPRIN0 ? 1'b1 : 1'bz;  // Controlled_Buffer controlled_buffer_8
  assign CBUS[21] = mxB0 ? 1'b1 : 1'bz;  // Controlled_Buffer controlled_buffer_9
  assign CBUS[22] = mxB1 ? 1'b1 : 1'bz;  // Controlled_Buffer controlled_buffer_10
  assign CBUS[0] = ldMAR ? 1'b1 : 1'bz;  // Controlled_Buffer controlled_buffer_11
  assign CFFBUS[3] = clADDR ? 1'b1 : 1'bz;  // Controlled_Buffer controlled_buffer_12
  assign CFFBUS[4] = stEXEC ? 1'b1 : 1'bz;  // Controlled_Buffer controlled_buffer_13
  assign rdMEM = rdMEM_t ? 1'b1 : 1'bz;  // Controlled_Buffer controlled_buffer_14

  // Other names for the same wires on the sheet: immed = ADDRBUS[0]; memdir = ADDRBUS[1]; memind = ADDRBUS[2];
  //   regind = ADDRBUS[3]; postincr = ADDRBUS[4]; postdec = ADDRBUS[5]; regdir = ADDRBUS[6]; ldPC = CBUS[3];
  //   incPC = CBUS[4]; ldIR7_0 = CBUS[5]; ldIR15_8 = CBUS[6]; ldIR23_16 = CBUS[7]; ldIR31_24 = CBUS[8];
  //   incSP = CBUS[11]; decSP = CBUS[12]; mxPC0 = CBUS[13]; mxPC1 = CBUS[14]; mxPC2 = CBUS[15]; mxGPRADR0 = CBUS[19];
  //   stFETCH = CFFBUS[0]; clFETCH = CFFBUS[1]; stADDR = CFFBUS[2]; clEXEC = CFFBUS[5]; stINTR = CFFBUS[6];
  //   clINTR = CFFBUS[7]; CLK = in_2; FCBUS = in_3; HALT = INSTRUCBUS[0]; RTS = INSTRUCBUS[1]; RTI = INSTRUCBUS[2];
  //   ROTR = INSTRUCBUS[3]; ROTRC = INSTRUCBUS[4]; PUSH = INSTRUCBUS[5]; POP = INSTRUCBUS[6]; BLEQ = INSTRUCBUS[7];
  //   BGREU = INSTRUCBUS[8]; BNNG = INSTRUCBUS[9]; BGRT = INSTRUCBUS[10]; JLEQ = INSTRUCBUS[11]; JSR = INSTRUCBUS[12];
  //   JMP = INSTRUCBUS[13]; LD = INSTRUCBUS[14]; ST = INSTRUCBUS[15]; ADD = INSTRUCBUS[16]; INC = INSTRUCBUS[17];
  //   LOR = INSTRUCBUS[18]; STRFIND = INSTRUCBUS[19]; grinst = INSTRUCBUS[20]; ADDR = PHASEFFBUS[1]; rst = in_1

  // Notes on the sheet:
  //   contents of rom_1 (hex, n*v repeats v):
  //   8000 c000 264001 184006 6 b0018 61 f0018 184082 184102 184302 702 274000 1b0018 61 1f0018 264801
  //   278000 841 7000
endmodule

module EXEC (
  input  in_1,
  input  in_2,
  input  in_3,
  input  [7:0] MDR,
  input  [15:0] PSW,
  input  [15:0] B,
  input  [3:0] PHASEFFBUS,
  input  [7:0] ADDRBUS,
  input  [20:0] INSTRUCBUS,
  output [15:0] A,
  output rdMEM,
  output [31:0] CBUS,
  output [15:0] ALU,
  output wrMEM,
  output [7:0] CFFBUS,
  output [11:0] CPSW
);

  wire ADDC, and_1_out, and_2_out, and_3_out, and_4_out, and_5_out, and_6_out, and_7_out, and_8_out, brchar,
       brcnd, brmul, brnotbrchar, brnotEXEC, brnotFCBUS, brnotGREU, brnotGRT, brnotLEQ, brnotNNG,
       brnotregdir, bruncnd, C, clEXEC, clPSWSTART, decSP, eqCHAR, eqZERO, incA, incGPR, incMAR, incSP, ldA,
       ldAUX, ldB, ldMAR, ldMDR, ldPC, ldPSWC, ldPSWI, ldPSWMDR, ldPSWN, ldPSWV, ldPSWZ, LEQ, mxA0, mxA1,
       mxA2, mxB0, mxB1, mxC0, mxC1, mxGPRIN1, mxMAR0, mxMAR1, mxMAR2, mxMDR0, mxMDR1, mxMDR2, mxMDR3, mxPC0,
       mxPC1, mxPC2, N, or_2_out, or_3_out, rdMEM_t, stINTR, V, wrGPR, wrMEM_t, xor_1_out, Z;
  wire [6:0] counter_1_q, kmopr_1_adr, multiplexer_3_out;
  wire [7:0] AUX_q;
  wire [14:0] multiplexer_5_out;
  wire [15:0] adder_1_out, multiplexer_2_out, multiplexer_4_out, or_1_out, shifter_1_out, subtractor_1_out;
  wire [51:41] rom_1_data;

  ROM #(.addrWidth(7), .dataWidth(52)) rom_1 (
    .addr(counter_1_q),
    .data({rom_1_data, clEXEC, stINTR, incA, mxMAR1, ldAUX, mxMDR3, incGPR, incMAR, mxGPRIN1, wrGPR, mxC0, mxPC2, mxMDR1, wrMEM_t, mxMDR2, mxMDR0, decSP, mxA2, mxC1, mxA1, mxA0, ldPSWI, ldPSWZ, ldPSWN, ldPSWV, ldPSWC, ldPSWMDR, ldA, mxB0, mxB1, ldB, mxPC0, mxPC1, ldPC, ldMDR, rdMEM_t, mxMAR2, mxMAR0, ldMAR, incSP, clPSWSTART}));
  Subtractor #(.width(16)) subtractor_1 (.a(A), .b(B), .out(subtractor_1_out));  // open: bin, bout
  assign or_1_out = B | A;  // OR_Gate or_1, 16 bits wide
  Shifter #(.shift("rr"), .width(16)) shifter_1 (.in(A), .\dist (4'b0001), .out(shifter_1_out));
  Multiplexer #(.enable("false"), .select(2)) multiplexer_1 (
    .in0(PSW[4]), .in1(ADDC), .in2(A[0]), .out(C), .sel({mxC1, mxC0}));  // open: in3
  Multiplexer #(.enable("false"), .width(16)) multiplexer_2 (
    .in0({16{1'b0}}), .in1(subtractor_1_out), .out(multiplexer_2_out), .sel(eqCHAR));
  Adder #(.width(16)) adder_1 (.a(B), .b(A), .out(adder_1_out), .cout(ADDC));  // open: cin
  Multiplexer #(.enable("false"), .width(7)) multiplexer_3 (
    .in0(rom_1_data[51:45]), .in1(kmopr_1_adr), .out(multiplexer_3_out), .sel(brmul));
  Multiplexer #(.enable("false"), .select(3), .width(16)) multiplexer_4 (
    .in0(B), .in1(adder_1_out), .in2(or_1_out), .in3(shifter_1_out), .in4({PSW[4], A[15:1]}),
    .in5(multiplexer_2_out), .out(multiplexer_4_out), .sel({mxA2, mxA1, mxA0}));  // open: in6, in7
  or or_2 (or_2_out, ldA, incA);
  Decoder #(.enable("false"), .select(4)) decoder_1 (
    .out1(bruncnd), .out2(brnotEXEC), .out3(brmul), .out4(brnotFCBUS), .out5(brnotLEQ), .out6(brnotGREU),
    .out7(brnotNNG), .out8(brnotGRT), .out9(brnotregdir), .out10(brnotbrchar), .sel(rom_1_data[44:41]));  // open: out0, out11, out12, out13, out14, out15
  Counter #(.max('h7f), .width(7)) counter_1 (
    .clr(in_1), .load(brcnd), .up(1'b1), .clk(in_2), .D(multiplexer_3_out), .Q(counter_1_q));  // open: count, carry
  Counter #(.max('hffff), .width(16)) AR (
    .clr(in_1), .load(ldA), .up(1'b1), .count(or_2_out), .clk(in_2), .D(multiplexer_4_out), .Q(A));  // open: carry
  and and_1 (and_1_out, brnotregdir, ~ADDRBUS[6]);  // AND_Gate
  and and_2 (and_2_out, brnotEXEC, ~PHASEFFBUS[2]);  // AND_Gate
  and and_3 (and_3_out, brnotFCBUS, ~in_3);  // AND_Gate
  and and_4 (and_4_out, brnotLEQ, ~LEQ);  // AND_Gate
  and and_5 (and_5_out, LEQ, brnotGRT);
  and and_6 (and_6_out, brnotGREU, PSW[4]);
  and and_7 (and_7_out, brnotNNG, PSW[2]);
  and and_8 (and_8_out, brnotbrchar, ~brchar);  // AND_Gate
  Multiplexer #(.enable("false"), .width(16)) multiplexer_5 (
    .in0(A), .in1(multiplexer_4_out), .out({N, multiplexer_5_out}), .sel(or_3_out));
  or or_3 (or_3_out, INSTRUCBUS[3], INSTRUCBUS[4]);
  or or_4 (brcnd, and_1_out, bruncnd, brmul, and_2_out, and_3_out, and_4_out, and_5_out, and_6_out, and_7_out, and_8_out);
  KMOPR kmopr_1 (
    .Adr(kmopr_1_adr), .JSR(INSTRUCBUS[12]), .JMP(INSTRUCBUS[13]), .LD(INSTRUCBUS[14]), .ST(INSTRUCBUS[15]),
    .ADD(INSTRUCBUS[16]), .RTS(INSTRUCBUS[1]), .INC(INSTRUCBUS[17]), .LOR(INSTRUCBUS[18]),
    .STRFIND(INSTRUCBUS[19]), .RTI(INSTRUCBUS[2]), .ROTR(INSTRUCBUS[3]), .ROTRC(INSTRUCBUS[4]),
    .PUSH(INSTRUCBUS[5]), .POP(INSTRUCBUS[6]), .BLEQ(INSTRUCBUS[7]), .HALT(INSTRUCBUS[0]),
    .BGREU(INSTRUCBUS[8]), .BNNG(INSTRUCBUS[9]), .BGRT(INSTRUCBUS[10]), .JLEQ(INSTRUCBUS[11]));
  and and_9 (V, ADDC, B[15], N);
  Register AUX (.D(A[7:0]), .en(ldAUX), .clk(in_2), .Q(AUX_q), .clr(in_1));
  Comparator #(.mode("unsigned")) comparator_1 (.a(MDR), .b(AUX_q), .eq(eqCHAR));  // open: gt, lt
  Comparator #(.mode("unsigned")) comparator_2 (.a(MDR), .b({8{1'b0}}), .eq(eqZERO));  // open: gt, lt
  or or_5 (LEQ, PSW[1], xor_1_out);
  xor xor_1 (xor_1_out, PSW[2], PSW[3]);
  or or_6 (brchar, eqCHAR, eqZERO);
  assign rdMEM = rdMEM_t ? 1'b1 : 1'bz;  // Controlled_Buffer controlled_buffer_1
  assign wrMEM = wrMEM_t ? 1'b1 : 1'bz;  // Controlled_Buffer controlled_buffer_2
  nor nor_1 (Z, multiplexer_5_out[0], multiplexer_5_out[1], multiplexer_5_out[2], multiplexer_5_out[3], multiplexer_5_out[4], multiplexer_5_out[5], multiplexer_5_out[6], multiplexer_5_out[7], multiplexer_5_out[8], multiplexer_5_out[9], multiplexer_5_out[10], multiplexer_5_out[11], multiplexer_5_out[12], multiplexer_5_out[13], multiplexer_5_out[14], N, 1'b0);
  assign CBUS[0] = ldMAR ? 1'b1 : 1'bz;  // Controlled_Buffer controlled_buffer_3
  assign CBUS[1] = incMAR ? 1'b1 : 1'bz;  // Controlled_Buffer controlled_buffer_4
  assign CBUS[2] = ldMDR ? 1'b1 : 1'bz;  // Controlled_Buffer controlled_buffer_5
  assign CBUS[3] = ldPC ? 1'b1 : 1'bz;  // Controlled_Buffer controlled_buffer_6
  assign CBUS[9] = ldB ? 1'b1 : 1'bz;  // Controlled_Buffer controlled_buffer_7
  assign CBUS[10] = wrGPR ? 1'b1 : 1'bz;  // Controlled_Buffer controlled_buffer_8
  assign CBUS[11] = incSP ? 1'b1 : 1'bz;  // Controlled_Buffer controlled_buffer_9
  assign CBUS[12] = decSP ? 1'b1 : 1'bz;  // Controlled_Buffer controlled_buffer_10
  assign CBUS[13] = mxPC0 ? 1'b1 : 1'bz;  // Controlled_Buffer controlled_buffer_11
  assign CBUS[14] = mxPC1 ? 1'b1 : 1'bz;  // Controlled_Buffer controlled_buffer_12
  assign CBUS[15] = mxPC2 ? 1'b1 : 1'bz;  // Controlled_Buffer controlled_buffer_13
  assign CBUS[16] = mxMAR0 ? 1'b1 : 1'bz;  // Controlled_Buffer controlled_buffer_14
  assign CBUS[17] = mxMAR1 ? 1'b1 : 1'bz;  // Controlled_Buffer controlled_buffer_15
  assign CBUS[18] = mxMAR2 ? 1'b1 : 1'bz;  // Controlled_Buffer controlled_buffer_16
  assign CBUS[21] = mxB0 ? 1'b1 : 1'bz;  // Controlled_Buffer controlled_buffer_17
  assign CBUS[22] = mxB1 ? 1'b1 : 1'bz;  // Controlled_Buffer controlled_buffer_18
  assign CBUS[23] = mxMDR0 ? 1'b1 : 1'bz;  // Controlled_Buffer controlled_buffer_19
  assign CBUS[24] = mxMDR1 ? 1'b1 : 1'bz;  // Controlled_Buffer controlled_buffer_20
  assign CBUS[25] = mxMDR2 ? 1'b1 : 1'bz;  // Controlled_Buffer controlled_buffer_21
  assign CBUS[26] = ldPSWMDR ? 1'b1 : 1'bz;  // Controlled_Buffer controlled_buffer_22
  assign CBUS[27] = incGPR ? 1'b1 : 1'bz;  // Controlled_Buffer controlled_buffer_23
  assign CBUS[28] = mxMDR3 ? 1'b1 : 1'bz;  // Controlled_Buffer controlled_buffer_24
  assign CBUS[29] = mxGPRIN1 ? 1'b1 : 1'bz;  // Controlled_Buffer controlled_buffer_25
  assign CFFBUS[6] = stINTR ? 1'b1 : 1'bz;  // Controlled_Buffer controlled_buffer_26
  assign CFFBUS[5] = clEXEC ? 1'b1 : 1'bz;  // Controlled_Buffer controlled_buffer_27
  assign CPSW[1] = clPSWSTART ? 1'b1 : 1'bz;  // Controlled_Buffer controlled_buffer_28
  assign CPSW[2] = ldPSWZ ? 1'b1 : 1'bz;  // Controlled_Buffer controlled_buffer_29
  assign CPSW[3] = ldPSWN ? 1'b1 : 1'bz;  // Controlled_Buffer controlled_buffer_30
  assign CPSW[4] = ldPSWV ? 1'b1 : 1'bz;  // Controlled_Buffer controlled_buffer_31
  assign CPSW[5] = ldPSWC ? 1'b1 : 1'bz;  // Controlled_Buffer controlled_buffer_32
  assign CPSW[6] = ldPSWI ? 1'b1 : 1'bz;  // Controlled_Buffer controlled_buffer_33
  assign CPSW[7] = Z ? 1'b1 : 1'bz;  // Controlled_Buffer controlled_buffer_34
  assign CPSW[8] = N ? 1'b1 : 1'bz;  // Controlled_Buffer controlled_buffer_35
  assign CPSW[9] = V ? 1'b1 : 1'bz;  // Controlled_Buffer controlled_buffer_36
  assign CPSW[10] = C ? 1'b1 : 1'bz;  // Controlled_Buffer controlled_buffer_37

  // Other names for the same wires on the sheet: brGREU = PSW[4]; PSWC = PSW[4]; immed = ADDRBUS[0];
  //   memdir = ADDRBUS[1]; memind = ADDRBUS[2]; regind = ADDRBUS[3]; postincr = ADDRBUS[4]; postdec = ADDRBUS[5];
  //   regdir = ADDRBUS[6]; graddr = ADDRBUS[7]; incPC = CBUS[4]; ldIR7_0 = CBUS[5]; ldIR15_8 = CBUS[6];
  //   ldIR23_16 = CBUS[7]; ldIR31_24 = CBUS[8]; mxGPRADR0 = CBUS[19]; mxGPRIN0 = CBUS[20]; stFETCH = CFFBUS[0];
  //   clFETCH = CFFBUS[1]; stADDR = CFFBUS[2]; clADDR = CFFBUS[3]; stEXEC = CFFBUS[4]; clINTR = CFFBUS[7]; CLK = in_2;
  //   stPSWSTART = CPSW[0]; I = CPSW[11]; FCBUS = in_3; HALT = INSTRUCBUS[0]; RTS = INSTRUCBUS[1];
  //   RTI = INSTRUCBUS[2]; ROTR = INSTRUCBUS[3]; ROTRC = INSTRUCBUS[4]; PUSH = INSTRUCBUS[5]; POP = INSTRUCBUS[6];
  //   BLEQ = INSTRUCBUS[7]; BGREU = INSTRUCBUS[8]; BNNG = INSTRUCBUS[9]; BGRT = INSTRUCBUS[10]; JLEQ = INSTRUCBUS[11];
  //   JSR = INSTRUCBUS[12]; JMP = INSTRUCBUS[13]; LD = INSTRUCBUS[14]; ST = INSTRUCBUS[15]; ADD = INSTRUCBUS[16];
  //   INC = INSTRUCBUS[17]; LOR = INSTRUCBUS[18]; STRFIND = INSTRUCBUS[19]; grinst = INSTRUCBUS[20];
  //   FETCH = PHASEFFBUS[0]; ADDR = PHASEFFBUS[1]; EXEC = PHASEFFBUS[2]; INTR = PHASEFFBUS[3]; PSWSTART = PSW[0];
  //   PSWZ = PSW[1]; brNNG = PSW[2]; PSWN = PSW[2]; PSWV = PSW[3]; PSWI = PSW[15]; rst = in_1

  // Notes on the sheet:
  //   contents of rom_1 (hex, n*v repeats v):
  //   40000000000 60000000000 a620000000001 2 1e a80000000060 19c e80000000060 a620000000280 2 1e
  //   1680000000060 c1e 1a80000000060 141e 2000 2080000000060 7c01e 2480000000060 8401e 2880000000060 19c
  //   2c80000000060 a620000000280 a62000076a000 a620000c6a000 100001c 6000040 3880008000000 1500005c
  //   3c80008000000 a620000000000 2 1e 4480000000060 141c 4880000000060 c00 2000 a620000060000
  //   a6a0000000000 a620000000380 a6c0000000000 a620000000380 a6e0000000000 a620000000380 a700000000000
  //   a620000000380 a6a0000000000 a620020000080 a620020000080 100001c 2000040 6a80008000000 100001c
  //   10000040 7080008000000 a620020000080 2000 a620000060000 4011a000 a620000060000 202000 a620000060000
  //   8520000000000 a620180000000 6000040 8680008000000 214000040 8a80008000000 a620000000000
  //   9320000000000 a620400000000 16000040 9480008000000 a00000040 9880008000000 a620000000000 1000002000
  //   200000001c a080000000020 9f44000000000 902000 38000000000
  //   Operaciona jedinica
  //   Upravljačka jedinica
endmodule

module INTR (
  input  rst,
  input  CLK,
  input  FCBUS,
  input  [3:0] PHASEFFBUS,
  input  [15:0] PSW,
  input  [3:0] intr3_0,
  input  [20:0] INSTRUCBUS,
  output [15:0] ADDIVTP,
  output [1:0] UEXT,
  output inta,
  output [31:0] CBUS,
  output [7:0] CFFBUS,
  output wrMEM,
  output rdMEM
);

  wire and_1_out, and_2_out, and_3_out, brcnd, brnotFCBUS, brnotINTR, brprekid, bruncnd, clINTR, decSP,
       incMAR, intrset, ldMAR, ldMDR, ldPC, mxMAR0, mxMAR1, mxMAR2, mxMDR0, mxMDR1, mxMDR2, mxPC0, mxPC1,
       nand_1_out, rdMEM_t, stFETCH, wrMEM_t;
  wire [4:0] counter_1_q;
  wire [15:0] register_1_q;
  wire [25:18] rom_1_data;

  ROM #(.addrWidth(5), .dataWidth(26)) rom_1 (
    .addr(counter_1_q),
    .data({rom_1_data, stFETCH, clINTR, inta, mxPC1, incMAR, mxPC0, ldPC, rdMEM_t, mxMAR1, mxMDR2, mxMDR1, wrMEM_t, mxMDR0, ldMDR, mxMAR2, mxMAR0, ldMAR, decSP}));
  // Priority_Encoder #(.select(2)) priority_encoder_1: pin names not known; wires that end beside it: UEXT, intrset
  Counter #(.max('h1f), .width(5)) counter_1 (
    .clr(rst), .load(brcnd), .up(1'b1), .clk(CLK), .D(rom_1_data[25:21]), .Q(counter_1_q));  // open: count, carry
  Register #(.width(16)) register_1 (.en(1'b0), .clk(CLK), .Q(register_1_q), .clr(rst));  // open: D
  Decoder #(.enable("false"), .select(3)) decoder_1 (
    .out1(bruncnd), .out2(brnotINTR), .out3(brprekid), .out4(brnotFCBUS), .sel(rom_1_data[20:18]));  // open: out0, out5, out6, out7
  Adder #(.width(16)) adder_1 (.a(register_1_q), .b({{13{1'b0}}, UEXT, 1'b0}), .out(ADDIVTP));  // open: cin, cout
  and and_1 (and_1_out, brnotINTR, ~PHASEFFBUS[3]);  // AND_Gate
  and and_2 (and_2_out, brprekid, nand_1_out);
  nand nand_1 (nand_1_out, PSW[15], intrset, ~INSTRUCBUS[0]);  // NAND_Gate
  and and_3 (and_3_out, brnotFCBUS, ~FCBUS);  // AND_Gate
  or or_1 (brcnd, bruncnd, and_1_out, and_2_out, and_3_out);
  assign CBUS[14] = mxPC1 ? 1'b1 : 1'bz;  // Controlled_Buffer controlled_buffer_1
  assign CBUS[16] = mxMAR0 ? 1'b1 : 1'bz;  // Controlled_Buffer controlled_buffer_2
  assign CBUS[23] = mxMDR0 ? 1'b1 : 1'bz;  // Controlled_Buffer controlled_buffer_3
  assign wrMEM = wrMEM_t ? 1'b1 : 1'bz;  // Controlled_Buffer controlled_buffer_4
  assign rdMEM = rdMEM_t ? 1'b1 : 1'bz;  // Controlled_Buffer controlled_buffer_5
  assign CBUS[2] = ldMDR ? 1'b1 : 1'bz;  // Controlled_Buffer controlled_buffer_6
  assign CBUS[3] = ldPC ? 1'b1 : 1'bz;  // Controlled_Buffer controlled_buffer_7
  assign CBUS[13] = mxPC0 ? 1'b1 : 1'bz;  // Controlled_Buffer controlled_buffer_8
  assign CBUS[17] = mxMAR1 ? 1'b1 : 1'bz;  // Controlled_Buffer controlled_buffer_9
  assign CBUS[18] = mxMAR2 ? 1'b1 : 1'bz;  // Controlled_Buffer controlled_buffer_10
  assign CFFBUS[0] = stFETCH ? 1'b1 : 1'bz;  // Controlled_Buffer controlled_buffer_11
  assign CFFBUS[7] = clINTR ? 1'b1 : 1'bz;  // Controlled_Buffer controlled_buffer_12
  assign CBUS[1] = incMAR ? 1'b1 : 1'bz;  // Controlled_Buffer controlled_buffer_13
  assign CBUS[12] = decSP ? 1'b1 : 1'bz;  // Controlled_Buffer controlled_buffer_14
  assign CBUS[24] = mxMDR1 ? 1'b1 : 1'bz;  // Controlled_Buffer controlled_buffer_15
  assign CBUS[0] = ldMAR ? 1'b1 : 1'bz;  // Controlled_Buffer controlled_buffer_16
  assign CBUS[25] = mxMDR2 ? 1'b1 : 1'bz;  // Controlled_Buffer controlled_buffer_17

  // Other names for the same wires on the sheet: ldBR = inta; incPC = CBUS[4]; ldIR7_0 = CBUS[5]; ldIR15_8 = CBUS[6];
  //   ldIR23_16 = CBUS[7]; ldIR31_24 = CBUS[8]; ldB = CBUS[9]; wrGPR = CBUS[10]; incSP = CBUS[11]; mxPC2 = CBUS[15];
  //   mxGPRADR0 = CBUS[19]; mxGPRIN0 = CBUS[20]; mxB0 = CBUS[21]; mxB1 = CBUS[22]; clFETCH = CFFBUS[1];
  //   stADDR = CFFBUS[2]; clADDR = CFFBUS[3]; stEXEC = CFFBUS[4]; clEXEC = CFFBUS[5]; stINTR = CFFBUS[6];
  //   HALT = INSTRUCBUS[0]; FETCH = PHASEFFBUS[0]; ADDR = PHASEFFBUS[1]; EXEC = PHASEFFBUS[2]; INTR = PHASEFFBUS[3];
  //   PSWSTART = PSW[0]; PSWZ = PSW[1]; PSWN = PSW[2]; PSWV = PSW[3]; PSWC = PSW[4]; PSWI = PSW[15]

  // Notes on the sheet:
  //   contents of rom_1 (hex, n*v repeats v):
  //   80000 26c0000 3f 700040 9f b00040 bf f00040 11f 1300040 13f 1700040 19f 1b00040 20a 1f00410 3800
  //   2300410 c800 70000
  //   Operaciona jedinica
  //   Upravljačka jedinica
endmodule

module RAM (
  input  [15:0] ADR,
  input  CLK,
  input  [7:0] DIN,
  input  WRMEM,
  input  RDMEM,
  input  rst,
  input  DEBUG,
  output [7:0] DOUT,
  output FCBUS
);

  wire and_1_out, and_2_out, and_3_out, CNT0, fc, LDCNT, not_1_out, notCNT0, or_1_out, or_2_out, s_r_ff_2_q,
       shift_register_1_p4, sl;
  wire [3:0] CNT, LFSR;

  S_R_Flip_Flop s_r_ff_1 (.S(rst), .R(1'b0), .clk(CLK), .Q(sl));  // open: reset, Qn, preset
  or or_1 (or_1_out, WRMEM, RDMEM);
  and and_1 (and_1_out, ~rst, sl);  // AND_Gate
  // Shift_Register #(.length(4)) shift_register_1: pin names not known; wires that end beside it: rst, and_1_out, CLK, shift_register_1_p4, 1'b1, 1'b1, 1'b1, 1'b1, LFSR[0], LFSR[1], LFSR[2], LFSR[3]
  // RisingEdge risingedge_1: pin names not known; wires that end beside it: or_1_out, CLK, LDCNT
  RAM_part #(.addrWidth(16), .asyncread("true")) ram_1 (
    .addr(ADR), .we(WRMEM), .oe(not_1_out), .clk(CLK), .din(DIN), .dout(DOUT));
  not not_1 (not_1_out, WRMEM);
  xor xor_1 (shift_register_1_p4, LFSR[2], LFSR[3]);
  and and_2 (and_2_out, CNT0, ~LDCNT);  // AND_Gate
  or or_2 (or_2_out, LDCNT, notCNT0);
  or or_3 (notCNT0, CNT[0], CNT[1], CNT[2], CNT[3]);
  not not_2 (CNT0, notCNT0);
  S_R_Flip_Flop s_r_ff_2 (.S(LDCNT), .R(and_2_out), .clk(CLK), .Q(s_r_ff_2_q), .reset(rst));  // open: Qn, preset
  Counter #(.max('hf), .width(4)) counter_1 (
    .load(LDCNT), .up(1'b0), .count(or_2_out), .clk(CLK), .D(LFSR), .Q(CNT));  // open: clr, carry
  and and_3 (and_3_out, s_r_ff_2_q, CNT0);
  or or_4 (FCBUS, fc, DEBUG);
  S_R_Flip_Flop s_r_ff_3 (.S(and_3_out), .R(fc), .clk(CLK), .Q(fc), .reset(rst));  // open: Qn, preset

  // Notes on the sheet:
  //   Shift registar za generisanje nasumičnog broja 
  //   Nasumičan broj predstavlja vreme pristupa memoriji
  //   Jedinica za generisanje function complete (fc) signala
  //   Brojač za dekrementiranje nasumičnog broja
endmodule
